// Digital circuit add-r.dig as structural Verilog
module add_r (
  input  [6:0] opcode,
  input  [2:0] funct3,
  input  [6:0] funct7,
  output eq
);

  wire add_2_eq, add_eq, r_type_eq;

  Comparator #(.Bits(7)) r_type (.a(opcode), .b(7'b0110011), .eq(r_type_eq));  // open: gt, lt
  Comparator #(.Bits(3)) add (.a(funct3), .b(3'b000), .eq(add_eq));  // open: gt, lt
  Comparator #(.Bits(7)) add_2 (.a(funct7), .b({7{1'b0}}), .eq(add_2_eq));  // open: gt, lt
  and and_1 (eq, r_type_eq, add_eq, add_2_eq);
endmodule
