// Digital circuit instruction_memory.dig as structural Verilog
module instruction_memory (
  input  [7:0] A,
  input  [3:0] PROG,
  output [31:0] D
);

  wire [31:0] unit_0_d, unit_1_d, unit_2_d, unit_3_d, unit_4_d, unit_5_d, unit_6_d, unit_7_d, unit_8_d,
       unit_9_d, unit_10_d, unit_11_d, unit_12_d, unit_13_d, unit_14_d;

  ROM #(.AddrBits(8), .Bits(32)) unit_0 (.A(A), .sel(1'b1), .D(unit_0_d));
  ROM #(.AddrBits(8), .Bits(32)) unit_1 (.A(A), .sel(1'b1), .D(unit_1_d));
  ROM #(.AddrBits(8), .Bits(32)) unit_2 (.A(A), .sel(1'b1), .D(unit_2_d));
  ROM #(.AddrBits(8), .Bits(32)) unit_3 (.A(A), .sel(1'b1), .D(unit_3_d));
  ROM #(.AddrBits(8), .Bits(32)) unit_4 (.A(A), .sel(1'b1), .D(unit_4_d));
  ROM #(.AddrBits(8), .Bits(32)) unit_5 (.A(A), .sel(1'b1), .D(unit_5_d));
  ROM #(.AddrBits(8), .Bits(32)) unit_6 (.A(A), .sel(1'b1), .D(unit_6_d));
  ROM #(.AddrBits(8), .Bits(32)) unit_7 (.A(A), .sel(1'b1), .D(unit_7_d));
  ROM #(.AddrBits(8), .Bits(32)) unit_8 (.A(A), .sel(1'b1), .D(unit_8_d));
  ROM #(.AddrBits(8), .Bits(32)) unit_9 (.A(A), .sel(1'b1), .D(unit_9_d));
  ROM #(.AddrBits(8), .Bits(32)) unit_10 (.A(A), .sel(1'b1), .D(unit_10_d));
  ROM #(.AddrBits(8), .Bits(32)) unit_11 (.A(A), .sel(1'b1), .D(unit_11_d));
  ROM #(.AddrBits(8), .Bits(32)) unit_12 (.A(A), .sel(1'b1), .D(unit_12_d));
  ROM #(.AddrBits(8), .Bits(32)) unit_13 (.A(A), .sel(1'b1), .D(unit_13_d));
  ROM #(.AddrBits(8), .Bits(32)) unit_14 (.A(A), .sel(1'b1), .D(unit_14_d));
  Multiplexer #(.Selector_Bits(4), .Bits(32)) multiplexer_1 (
    .sel(PROG), .in_0(unit_0_d), .in_1(unit_1_d), .in_2(unit_2_d), .in_3(unit_3_d), .in_4(unit_4_d),
    .in_5(unit_5_d), .in_6(unit_6_d), .in_7(unit_7_d), .in_8(unit_8_d), .in_9(unit_9_d), .in_10(unit_10_d),
    .in_11(unit_11_d), .in_12(unit_12_d), .in_13(unit_13_d), .in_14(unit_14_d), .in_15({32{1'b0}}), .out(D));

  // Notes on the sheet:
  //   contents of unit_0 (hex, n*v repeats v):
  //   100513,250513,c0001073
  //   contents of unit_1 (hex, n*v repeats v):
  //   300513,600593,b50533,c0001073
  //   contents of unit_2 (hex, n*v repeats v):
  //   100513,200593,8000ef,c0001073,b50533,8067
  //   contents of unit_3 (hex, n*v repeats v):
  //   300513,700593,2b50533,c0001073
  //   contents of unit_4 (hex, n*v repeats v):
  //   100593,200613,c59533,c0001073
  //   contents of unit_5 (hex, n*v repeats v):
  //   800593,100613,c5d533,c0001073
  //   contents of unit_6 (hex, n*v repeats v):
  //   100593,359513,c0001073
  //   contents of unit_7 (hex, n*v repeats v):
  //   2000593,25d513,c0001073
  //   contents of unit_8 (hex, n*v repeats v):
  //   100513,80006f,513,c0001073
  //   contents of unit_9 (hex, n*v repeats v):
  //   100513,100593,b50463,513,c0001073
  //   contents of unit_10 (hex, n*v repeats v):
  //   100513,200593,b54463,513,c0001073
  //   contents of unit_11 (hex, n*v repeats v):
  //   200513,100593,b55463,513,c0001073
  //   contents of unit_12 (hex, n*v repeats v):
  //   8000113,ff810113,513,6300293,513023,13503,c0001073
  //   contents of unit_13 (hex, n*v repeats v):
  //   8000113,ff810113,513,6300293,512023,12503,c0001073
  //   contents of unit_14 (hex, n*v repeats v):
  //   8000113,ff810113,513,6300293,5101a3,310503,c0001073
endmodule
