// Digital circuit lb-decoder.dig as structural Verilog
module lb_decoder (
  input  [63:0] D,
  input  [2:0] Boff,
  output [63:0] Dlb
);

  Multiplexer #(.Selector_Bits(3), .Bits(8)) multiplexer_1 (
    .sel(Boff), .in_0(D[7:0]), .in_1(D[15:8]), .in_2(D[23:16]), .in_3(D[31:24]), .in_4(D[39:32]),
    .in_5(D[47:40]), .in_6(D[55:48]), .in_7(D[63:56]), .out(Dlb[7:0]));
  // Pins of 1 and 64 bits meet at {{56{1'b0}}, Dlb[7:0]}

  assign Dlb[63:8] = {56{1'b0}};
endmodule
